// Logisim project Lab 1.circ as structural Verilog: 1 circuit, main circuit main
module main (
  input  MotionDetected,
  input  LightDetected,
  output LampOn
);

  wire not_1_out;

  not not_1 (not_1_out, LightDetected);
  and and_1 (LampOn, MotionDetected, not_1_out);

  // Notes on the sheet:
  //   M
  //   L
  //   M~L
  //   A
endmodule
