// Logisim project Lab 11.circ as structural Verilog: 10 circuits, main circuit main
module main (
  input  [15:0] in_1,
  input  START,
  input  RESET,
  output READY
);

  wire clock_1_out, control_unit_1_write_enable;
  wire [2:0] datapath_1_pzn;
  wire [3:0] control_unit_1_constant_out, datapath_1_addrout, datapath_1_dataout, ram_1_data;
  wire [15:0] control_unit_1_ctrl_word;

  Clock clock_1 (.out(clock_1_out));
  Datapath datapath_1 (
    .CLK(clock_1_out), .ConstIn(control_unit_1_constant_out), .Control_Word(control_unit_1_ctrl_word),
    .AddrOut(datapath_1_addrout), .DataOut(datapath_1_dataout), .PZN(datapath_1_pzn), .DataIn(ram_1_data));
  Control_Unit control_unit_1 (
    .Start(START), .Reset(RESET), .PZN(datapath_1_pzn), .Write_Enable(control_unit_1_write_enable),
    .Ready(READY), .Instruction(in_1), .CONSTANT_OUT(control_unit_1_constant_out),
    .CTRL_WORD(control_unit_1_ctrl_word), .CLK(clock_1_out));
  RAM #(.addrWidth(4), .dataWidth(4), .bus("separate")) ram_1 (
    .addr(datapath_1_addrout), .din(datapath_1_dataout), .data(ram_1_data),
    .str(control_unit_1_write_enable), .clk(clock_1_out));  // open: sel, ld, clr

  // Notes on the sheet:
  //   DATAPATH
  //   CONTROL UNIT
endmodule

module RegFile (
  input  [3:0] Din,
  input  Load,
  input  [2:0] AA,
  input  [2:0] DA,
  input  [2:0] BB,
  input  CLK,
  output [3:0] A_Out,
  output [3:0] B_Out
);

  wire and_1_out, and_2_out, and_3_out, and_4_out, and_5_out, and_6_out, and_7_out, and_8_out,
       decoder_1_out0, decoder_1_out1, decoder_1_out2, decoder_1_out3, decoder_1_out4, decoder_1_out5,
       decoder_1_out6, decoder_1_out7;
  wire [3:0] register_1_q, register_2_q, register_3_q, register_4_q, register_5_q, register_6_q,
       register_7_q, register_8_q;

  Decoder #(.select(3)) decoder_1 (
    .out0(decoder_1_out0), .out1(decoder_1_out1), .out2(decoder_1_out2), .out3(decoder_1_out3),
    .out4(decoder_1_out4), .out5(decoder_1_out5), .out6(decoder_1_out6), .out7(decoder_1_out7), .sel(DA));  // open: en
  and and_1 (and_1_out, Load, decoder_1_out0);
  and and_2 (and_2_out, Load, decoder_1_out1);
  and and_3 (and_3_out, Load, decoder_1_out2);
  and and_4 (and_4_out, Load, decoder_1_out3);
  and and_5 (and_5_out, Load, decoder_1_out4);
  and and_6 (and_6_out, Load, decoder_1_out5);
  and and_7 (and_7_out, Load, decoder_1_out6);
  and and_8 (and_8_out, Load, decoder_1_out7);
  Register #(.width(4)) register_1 (.D(Din), .en(and_1_out), .Q(register_1_q), .clk(CLK), .clr(1'b0));
  Register #(.width(4)) register_2 (.D(Din), .en(and_2_out), .Q(register_2_q), .clk(CLK), .clr(1'b0));
  Register #(.width(4)) register_3 (.D(Din), .en(and_3_out), .Q(register_3_q), .clk(CLK), .clr(1'b0));
  Register #(.width(4)) register_4 (.D(Din), .en(and_4_out), .Q(register_4_q), .clk(CLK), .clr(1'b0));
  Register #(.width(4)) register_5 (.D(Din), .en(and_5_out), .Q(register_5_q), .clk(CLK), .clr(1'b0));
  Register #(.width(4)) register_6 (.D(Din), .en(and_6_out), .Q(register_6_q), .clk(CLK), .clr(1'b0));
  Register #(.width(4)) register_7 (.D(Din), .en(and_7_out), .Q(register_7_q), .clk(CLK), .clr(1'b0));
  Register #(.width(4)) register_8 (.D(Din), .en(and_8_out), .Q(register_8_q), .clk(CLK), .clr(1'b0));
  Multiplexer #(.select(3), .width(4)) multiplexer_1 (
    .in0(register_1_q), .in1(register_2_q), .in2(register_3_q), .in3(register_4_q), .in4(register_5_q),
    .in5(register_6_q), .in6(register_7_q), .in7(register_8_q), .out(A_Out), .sel(AA));  // open: en
  Multiplexer #(.select(3), .width(4)) multiplexer_2 (
    .in0(register_1_q), .in1(register_2_q), .in2(register_3_q), .in3(register_4_q), .in4(register_5_q),
    .in5(register_6_q), .in6(register_7_q), .in7(register_8_q), .out(B_Out), .sel(BB));  // open: en
endmodule

module FunctionSelect (
  input  [3:0] A_In,
  input  [3:0] B_In,
  input  [3:0] FS,
  output [2:0] PZN,
  output [3:0] Data_Out
);

  wire [3:0] adder_1_out, adder_2_out, and_1_out, divider_1_out, multiplier_1_out, not_1_out, or_1_out,
       shifter_1_out, shifter_2_out, shifter_3_out, subtractor_1_out;

  assign not_1_out = ~A_In;  // NOT_Gate not_1, 4 bits wide
  Adder #(.width(4)) adder_1 (.a(A_In), .b(B_In), .out(adder_1_out));  // open: cin, cout
  Subtractor #(.width(4)) subtractor_1 (.a(A_In), .b(B_In), .out(subtractor_1_out));  // open: bin, bout
  Multiplier #(.width(4)) multiplier_1 (.a(A_In), .b(B_In), .out(multiplier_1_out));  // open: cin, cout
  Divider #(.width(4)) divider_1 (.a(A_In), .b(B_In), .out(divider_1_out));  // open: upper, rem
  assign and_1_out = A_In & B_In;  // AND_Gate and_1, 4 bits wide
  assign or_1_out = A_In | B_In;  // OR_Gate or_1, 4 bits wide
  Adder #(.width(4)) adder_2 (.a(not_1_out), .b(4'b0001), .out(adder_2_out));  // open: cin, cout
  Shifter #(.width(4), .shift("lr")) shifter_1 (.in(A_In), .\dist (2'b01), .out(shifter_1_out));
  Shifter #(.width(4)) shifter_2 (.in(A_In), .\dist (2'b01), .out(shifter_2_out));
  Shifter #(.width(4), .shift("ar")) shifter_3 (.in(A_In), .\dist (2'b01), .out(shifter_3_out));
  Multiplexer #(.select(4), .width(4)) multiplexer_1 (
    .in0(4'b0000), .in1(4'b0001), .in2(A_In), .in3(B_In), .in4(adder_1_out), .in5(subtractor_1_out),
    .in6(multiplier_1_out), .in7(divider_1_out), .in8(not_1_out), .in9(and_1_out), .in10(or_1_out),
    .in11(adder_2_out), .in12(shifter_1_out), .in13(shifter_2_out), .in14(shifter_3_out), .out(Data_Out),
    .sel(FS));  // open: in15, en
  and and_2 (PZN[1], ~Data_Out[0], ~Data_Out[1], ~Data_Out[2], ~Data_Out[3]);  // AND_Gate
  and and_3 (PZN[2], ~PZN[1], ~Data_Out[3]);  // AND_Gate

  assign PZN[0] = Data_Out[3];
endmodule

module CAR (
  input  LOAD,
  input  [7:0] CAL,
  input  RESET,
  input  CLK,
  output [7:0] CA
);

  wire counter_2_q, not_1_out;

  not not_1 (not_1_out, LOAD);
  Counter counter_1 (.load(LOAD), .D(CAL), .count(not_1_out), .Q(CA), .clk(CLK), .clr(counter_2_q));  // open: carry
  Counter #(.width(1), .max('h1)) counter_2 (
    .count(RESET), .Q(counter_2_q), .clk(CLK), .clr(counter_2_q));  // open: load, D, carry
endmodule

module Datapath (
  input  CLK,
  input  [3:0] ConstIn,
  input  [15:0] Control_Word,
  input  [3:0] DataIn,
  output [3:0] AddrOut,
  output [3:0] DataOut,
  output [2:0] PZN
);

  wire [2:0] functionselect_1_pzn;
  wire [3:0] functionselect_1_data_out, multiplexer_2_out, regfile_1_b_out;

  Multiplexer #(.width(4), .enable("false")) multiplexer_1 (
    .in0(regfile_1_b_out), .in1(ConstIn), .out(DataOut), .sel(Control_Word[12]));
  FunctionSelect functionselect_1 (
    .A_In(AddrOut), .B_In(DataOut), .FS(Control_Word[7:4]), .PZN(functionselect_1_pzn),
    .Data_Out(functionselect_1_data_out));
  Multiplexer #(.width(4), .enable("false")) multiplexer_2 (
    .in0(functionselect_1_data_out), .in1(DataIn), .out(multiplexer_2_out), .sel(Control_Word[8]));
  RegFile regfile_1 (
    .Din(multiplexer_2_out), .Load(Control_Word[0]), .AA(Control_Word[15:13]), .DA(Control_Word[3:1]),
    .BB(Control_Word[11:9]), .CLK(CLK), .A_Out(AddrOut), .B_Out(regfile_1_b_out));
  Register #(.width(3)) register_1 (.D(functionselect_1_pzn), .Q(PZN), .clk(CLK));  // open: en, clr

  // Notes on the sheet:
  //   MB
  //   MF
endmodule

module Control_Unit (
  input  [15:0] Instruction,
  input  [2:0] PZN,
  input  Start,
  input  Reset,
  input  CLK,
  output [3:0] CONSTANT_OUT,
  output Write_Enable,
  output [15:0] CTRL_WORD,
  output Ready
);

  wire pzn_1_load;
  wire [7:0] car_1_ca, data_signal_logic_1_data_out, not_1_out;
  wire [17:17] rom_1_data;

  Operand_Select operand_select_1 (
    .Op_A(Instruction[11:8]), .Op_B(Instruction[7:4]), .Op_C(Instruction[3:0]), .Select(CTRL_WORD[11:9]),
    .Const(CONSTANT_OUT));
  PZN pzn_1 (
    .START(Start), .READY(Ready), .CAR(car_1_ca), .PZN(PZN), .CONDITION(CTRL_WORD[14:12]),
    .MODE(rom_1_data[17]), .LOAD(pzn_1_load));
  Data_Signal_Logic data_signal_logic_1 (
    .OPCODE(Instruction[15:12]), .NEXT_ADDRESS(CTRL_WORD[11:4]), .Start(Start), .Ready(Ready),
    .Data_Out(data_signal_logic_1_data_out));
  CAR car_1 (.LOAD(pzn_1_load), .CAL(data_signal_logic_1_data_out), .RESET(Reset), .CLK(CLK), .CA(car_1_ca));
  assign not_1_out = ~car_1_ca;  // NOT_Gate not_1, 8 bits wide
  ROM #(.dataWidth(18)) rom_1 (.addr(car_1_ca), .data({rom_1_data[17], Write_Enable, CTRL_WORD}));  // open: sel
  and and_1 (Ready, not_1_out[0], not_1_out[1], not_1_out[2], not_1_out[3], not_1_out[4], not_1_out[5], not_1_out[6], not_1_out[7]);

  // Notes on the sheet:
  //   OP CODE
  //   OP A
  //   OP C
  //   OP B
  //   NEXT ADDRESS
  //   CONDITION
  //   MODE
  //   contents of rom_1 (hex, n*v repeats v):
  //   27000 15*0 1231 1433 10200 27000 12*0 1231 1433 2105 10400 27000 11*0 1231 1433 1635 2107 4109 684b
  //   10a00 27000 8*0 1231 1433 1635 2107 4109 685b 10a00 27000 8*0 1231 1433 1635 2107 4109 686b 10a00
  //   27000 8*0 1231 1433 2105 40c7 10600 27000 10*0 1231 1433 2105 4087 10600 27000 10*0 1231 1433 1635
  //   2107 4109 689b 10a00 27000 8*0 1231 1433 1635 4107 6027 25000 2103 10200 27000 7*0 1231 1433 1635
  //   2103 4105 4257 22aa0 15 10800 27000 5 10800 27000 0 0 0 1231 1633 105 2107 4649 1b a0db a0db 8a5d
  //   23bc0 10000 27000 12200 27000
endmodule

module Data_Signal_Logic (
  input  [3:0] OPCODE,
  input  [7:0] NEXT_ADDRESS,
  input  Start,
  input  Ready,
  output [7:0] Data_Out
);

  wire and_1_out;

  and and_1 (and_1_out, Start, Ready);
  Multiplexer #(.width(8)) multiplexer_1 (
    .in0(NEXT_ADDRESS), .in1({OPCODE, 4'b0000}), .out(Data_Out), .sel(and_1_out));  // open: en
endmodule

module Operand_Select (
  input  [3:0] Op_A,
  input  [3:0] Op_B,
  input  [3:0] Op_C,
  input  [2:0] Select,
  output [3:0] Const
);

  Multiplexer #(.select(3), .width(4)) multiplexer_1 (
    .in0(4'b0000), .in1(Op_A), .in2(Op_B), .in3(Op_C), .in4(4'b0000), .in5(4'b0000), .in6(4'b0000),
    .in7(4'b0000), .out(Const), .sel(Select));  // open: en
endmodule

module PZN (
  input  START,
  input  READY,
  input  [7:0] CAR,
  input  [2:0] PZN,
  input  [2:0] CONDITION,
  input  MODE,
  output LOAD
);

  wire and_1_out, and_2_out, and_3_out, pzn_select_1_condition_met;
  wire [7:0] not_1_out;

  assign not_1_out = ~CAR;  // NOT_Gate not_1, 8 bits wide
  and and_1 (and_1_out, not_1_out[0], not_1_out[1], not_1_out[2], not_1_out[3], not_1_out[4], not_1_out[5], not_1_out[6], not_1_out[7]);
  PZN_Select pzn_select_1 (.PZN(PZN), .Condition(CONDITION), .Condition_Met(pzn_select_1_condition_met));
  and and_2 (and_2_out, START, READY, and_1_out);
  and and_3 (and_3_out, pzn_select_1_condition_met, MODE);
  or or_1 (LOAD, and_2_out, and_3_out);
endmodule

module PZN_Select (
  input  [2:0] PZN,
  input  [2:0] Condition,
  output Condition_Met
);

  wire or_1_out, or_2_out, or_3_out;

  or or_1 (or_1_out, PZN[0], PZN[1]);
  or or_2 (or_2_out, PZN[0], PZN[2]);
  or or_3 (or_3_out, PZN[1], PZN[2]);
  Multiplexer #(.select(3)) multiplexer_1 (
    .in0(1'b0), .in1(PZN[0]), .in2(PZN[1]), .in3(or_1_out), .in4(PZN[2]), .in5(or_2_out), .in6(or_3_out),
    .in7(1'b1), .out(Condition_Met), .sel(Condition));  // open: en
endmodule
