// Logisim project Lab 2.circ as structural Verilog: 1 circuit, main circuit main
module main (
  input  A,
  input  B,
  input  C,
  input  D,
  output P,
  output T
);

  wire A_nB_nCD_out, A_nBC_nD_out, A_nBCD_out, AB_nC_nD_out, AB_nCD_out, ABC_nD_out, nA_nBCD_out, nA_out,
       nAB_nCD_out, nABC_nD_out, nABCD_out, nB_out, nC_out, nD_out;

  not nA (nA_out, A);
  not nB (nB_out, B);
  not nC (nC_out, C);
  not nD (nD_out, D);
  and nA_nBCD (nA_nBCD_out, nA_out, nB_out, C, D);
  and nAB_nCD (nAB_nCD_out, nA_out, B, nC_out, D);
  and nABC_nD (nABC_nD_out, nA_out, B, C, nD_out);
  and A_nB_nCD (A_nB_nCD_out, A, nB_out, nC_out, D);
  and A_nBC_nD (A_nBC_nD_out, A, nB_out, C, nD_out);
  and AB_nC_nD (AB_nC_nD_out, A, B, nC_out, nD_out);
  and nABCD (nABCD_out, nA_out, B, C, D);
  and A_nBCD (A_nBCD_out, A, nB_out, C, D);
  and AB_nCD (AB_nCD_out, A, B, nC_out, D);
  and ABC_nD (ABC_nD_out, A, B, C, nD_out);
  or or_1 (P, nA_nBCD_out, nAB_nCD_out, nABC_nD_out, A_nB_nCD_out, A_nBC_nD_out, AB_nC_nD_out);
  or or_2 (T, nABCD_out, A_nBCD_out, AB_nCD_out, ABC_nD_out);
endmodule
