// Logisim project Lab 4.circ as structural Verilog
module Design__0 (
  input  A0,
  input  A1,
  input  B0,
  input  B1,
  output C0,
  output C1
);

  wire and_1_out, and_2_out, and_3_out, and_4_out, not_1_out, not_2_out;

  not not_1 (not_1_out, A1);
  not not_2 (not_2_out, B1);
  and and_1 (and_1_out, not_1_out, B0);
  and and_2 (and_2_out, B1, B0);
  and and_3 (and_3_out, A0, not_2_out);
  and and_4 (and_4_out, A1, A0);
  or or_1 (C1, B1, A1);
  or or_2 (C0, and_1_out, and_2_out, and_3_out, and_4_out);
endmodule

module Design__1 (
  input  [3:0] A1_A0_B1_B0,
  output C0,
  output C1
);

  Multiplexer #(.select(4), .enable("false")) multiplexer_1 (
    .in0(1'b0), .in1(1'b1), .in2(1'b0), .in3(1'b1), .in4(1'b1), .in5(1'b1), .in6(1'b0), .in7(1'b1),
    .in8(1'b0), .in9(1'b0), .in10(1'b0), .in11(1'b1), .in12(1'b1), .in13(1'b1), .in14(1'b1), .in15(1'b1),
    .out(C0), .sel(A1_A0_B1_B0));
  Multiplexer #(.select(4), .enable("false")) multiplexer_2 (
    .in0(1'b0), .in1(1'b0), .in2(1'b1), .in3(1'b1), .in4(1'b0), .in5(1'b0), .in6(1'b1), .in7(1'b1),
    .in8(1'b1), .in9(1'b1), .in10(1'b1), .in11(1'b1), .in12(1'b1), .in13(1'b1), .in14(1'b1), .in15(1'b1),
    .out(C1), .sel(A1_A0_B1_B0));
endmodule

module Design__2 (
  input  A0,
  input  A1,
  input  B0,
  input  B1,
  output C0,
  output C1
);

  wire multiplexer_2_out, multiplexer_3_out;

  Multiplexer #(.enable("false")) multiplexer_1 (.in0(A1), .in1(B1), .out(C1), .sel(B1));
  Multiplexer #(.enable("false")) multiplexer_2 (.in0(A0), .in1(B0), .out(multiplexer_2_out), .sel(B1));
  Multiplexer #(.enable("false")) multiplexer_3 (.in0(B0), .in1(A0), .out(multiplexer_3_out), .sel(A1));
  Multiplexer #(.enable("false")) multiplexer_4 (
    .in0(multiplexer_2_out), .in1(1'b1), .out(C0), .sel(multiplexer_3_out));
endmodule

module Design__3 (
  input  A0,
  input  A1,
  input  B0,
  input  B1,
  output C0,
  output C1
);

  wire nand_1_out, nand_2_out, nand_3_out, nand_4_out, nand_5_out, nand_6_out, nand_7_out, nand_8_out;

  nand nand_1 (nand_1_out, A1, A1);
  nand nand_2 (nand_2_out, B1, B1);
  nand nand_3 (nand_3_out, B1, B1);
  nand nand_4 (nand_4_out, A1, A1);
  nand nand_5 (nand_5_out, nand_1_out, B0);
  nand nand_6 (nand_6_out, B0, B1);
  nand nand_7 (nand_7_out, A0, nand_2_out);
  nand nand_8 (nand_8_out, A0, A1);
  nand nand_9 (C1, nand_3_out, nand_4_out);
  nand nand_10 (C0, nand_5_out, nand_6_out, nand_7_out, nand_8_out);
endmodule

module Design__4 (
  input  A,
  input  B,
  input  Am,
  input  Bm,
  output C,
  output Amo,
  output Bmo
);

  wire and_1_out, and_2_out, and_3_out, and_4_out, and_5_out, and_6_out, and_7_out, and_8_out, and_9_out,
       and_10_out, not_1_out, not_2_out, not_3_out, not_4_out, not_5_out, not_6_out, not_7_out, not_8_out,
       not_9_out, not_10_out;

  and and_1 (and_1_out, B, not_1_out);
  not not_1 (not_1_out, Am);
  and and_2 (and_2_out, B, Bm);
  and and_3 (and_3_out, A, not_2_out);
  not not_2 (not_2_out, Bm);
  and and_4 (and_4_out, A, Am);
  and and_5 (and_5_out, Am, not_3_out);
  not not_3 (not_3_out, Bm);
  not not_4 (not_4_out, B);
  and and_6 (and_6_out, A, not_4_out, not_5_out);
  not not_5 (not_5_out, Bm);
  and and_7 (and_7_out, A, not_6_out, Am);
  not not_6 (not_6_out, B);
  not not_7 (not_7_out, Am);
  and and_8 (and_8_out, not_7_out, Bm);
  not not_8 (not_8_out, A);
  and and_9 (and_9_out, not_8_out, B, not_9_out);
  not not_9 (not_9_out, Am);
  not not_10 (not_10_out, A);
  and and_10 (and_10_out, not_10_out, B, Bm);
  or or_1 (C, and_1_out, and_2_out, and_3_out, and_4_out);
  or or_2 (Amo, and_5_out, and_6_out, and_7_out);
  or or_3 (Bmo, and_8_out, and_9_out, and_10_out);
endmodule

module Design__5 (
  input  A3,
  input  A2,
  input  A1,
  input  A0,
  input  B3,
  input  B2,
  input  B1,
  input  B0,
  output [3:0] out_9
);

  wire design_4_1_amo, design_4_1_bmo, design_4_2_amo, design_4_2_bmo, design_4_3_amo, design_4_3_bmo;

  Design__4 design_4_1 (.A(A3), .B(B3), .C(out_9[3]), .Am(A3), .Bm(B3), .Amo(design_4_1_amo), .Bmo(design_4_1_bmo));
  Design__4 design_4_2 (
    .A(A2), .B(B2), .C(out_9[2]), .Am(design_4_1_amo), .Bm(design_4_1_bmo), .Amo(design_4_2_amo),
    .Bmo(design_4_2_bmo));
  Design__4 design_4_3 (
    .A(A1), .B(B1), .C(out_9[1]), .Am(design_4_2_amo), .Bm(design_4_2_bmo), .Amo(design_4_3_amo),
    .Bmo(design_4_3_bmo));
  Design__4 design_4_4 (.A(A0), .B(B0), .C(out_9[0]), .Am(design_4_3_amo), .Bm(design_4_3_bmo));  // open: Amo, Bmo
endmodule
