// Logisim project Lab 5.circ as structural Verilog: 3 circuits, main circuit Figure 1
module Figure_1 (
  input  IN,
  output SHOT
);

  wire CLK_out, d_ff_1_q;

  Clock CLK (.out(CLK_out));
  D_Flip_Flop d_ff_1 (.clk(CLK_out), .D(SHOT), .Q(d_ff_1_q));  // open: Qn, preset, en, reset
  or IN___Q (SHOT, IN, d_ff_1_q);
endmodule

module Figure_2 (
  input  E,
  output T
);

  wire CLK_out, d_ff_1_qn, nEQ___nQE_out, nEQ_out, not_1_out, nQE_out;

  Clock CLK (.out(CLK_out));
  D_Flip_Flop d_ff_1 (.clk(CLK_out), .D(nEQ___nQE_out), .Q(T), .Qn(d_ff_1_qn));  // open: preset, en, reset
  not not_1 (not_1_out, E);
  and nEQ (nEQ_out, not_1_out, T);
  and nQE (nQE_out, d_ff_1_qn, E);
  or nEQ___nQE (nEQ___nQE_out, nEQ_out, nQE_out);
endmodule

module Figure_3 (
  input  X,
  output UNLOCK
);

  wire clock_1_out, d_ff_1_q, d_ff_1_qn, d_ff_2_q, d_ff_2_qn, not_1_out, nQ0Q1_out, nXQ1_out,
       Q0_nQ1___nXQ1_out, X_nQ0___XQ1___nQ0Q1_out, X_nQ0_out, XQ1_out;

  Clock clock_1 (.out(clock_1_out));
  not not_1 (not_1_out, X);
  D_Flip_Flop d_ff_1 (
    .clk(clock_1_out), .D(Q0_nQ1___nXQ1_out), .Q(d_ff_1_q), .Qn(d_ff_1_qn));  // open: preset, en, reset
  D_Flip_Flop d_ff_2 (
    .clk(clock_1_out), .D(X_nQ0___XQ1___nQ0Q1_out), .Q(d_ff_2_q), .Qn(d_ff_2_qn));  // open: preset, en, reset
  and X_nQ0 (X_nQ0_out, X, d_ff_1_qn);
  and XQ1 (XQ1_out, X, d_ff_2_q);
  and nQ0Q1 (nQ0Q1_out, d_ff_2_q, d_ff_1_qn);
  and Q0_nQ1 (UNLOCK, d_ff_2_qn, d_ff_1_q);
  and nXQ1 (nXQ1_out, d_ff_2_q, not_1_out);
  or X_nQ0___XQ1___nQ0Q1 (X_nQ0___XQ1___nQ0Q1_out, X_nQ0_out, XQ1_out, nQ0Q1_out);
  or Q0_nQ1___nXQ1 (Q0_nQ1___nXQ1_out, UNLOCK, nXQ1_out);

  // Notes on the sheet:
  //   Q0
  //   Q1
  //   Q0~Q1
endmodule
