// Logisim project Lab 6.circ as structural Verilog: 1 circuit, main circuit main
module main (
  input  B,
  input  A,
  input  ENABLE,
  output VALID,
  output DIRECTION
);

  wire and_1_out, and_2_out, and_4_out, and_5_out, and_6_out, and_7_out, and_8_out, and_9_out, and_10_out,
       and_11_out, and_12_out, and_13_out, and_14_out, and_15_out, and_16_out, and_17_out, and_18_out,
       and_19_out, and_20_out, clock_1_out, D0_out, D1_out, D2_out, not_1_out, not_2_out, or_1_out, or_2_out,
       or_3_out, or_4_out, Q0_q, Q0_qn, Q1_q, Q1_qn, Q2_q, Q2_qn;

  Clock clock_1 (.out(clock_1_out));
  not not_1 (not_1_out, B);
  not not_2 (not_2_out, A);
  D_Flip_Flop Q0 (.clk(clock_1_out), .D(D0_out), .Q(Q0_q), .Qn(Q0_qn));  // open: preset, en, reset
  D_Flip_Flop Q1 (.clk(clock_1_out), .D(D1_out), .Q(Q1_q), .Qn(Q1_qn));  // open: preset, en, reset
  D_Flip_Flop Q2 (.clk(clock_1_out), .D(D2_out), .Q(Q2_q), .Qn(Q2_qn));  // open: preset, en, reset
  and and_1 (and_1_out, Q1_qn, Q0_q);
  or or_1 (or_1_out, and_1_out, and_2_out);
  and and_2 (and_2_out, Q1_q, Q0_qn);
  and and_3 (DIRECTION, Q2_qn, Q1_qn, Q0_q);
  and and_4 (and_4_out, Q2_qn, Q1_qn, Q0_q);
  and and_5 (and_5_out, Q2_qn, Q1_qn, B);
  and and_6 (and_6_out, Q2_q, Q1_qn, Q0_q, not_2_out);
  and and_7 (and_7_out, Q2_q, Q0_q, not_2_out, B);
  and and_8 (and_8_out, Q2_q, Q1_q, A, B);
  and and_9 (and_9_out, Q2_q, Q1_qn, Q0_qn, A, not_1_out);
  and and_10 (and_10_out, Q1_q, Q0_qn, not_2_out, not_1_out);
  and and_11 (and_11_out, Q2_qn, Q1_q, Q0_qn, not_2_out);
  and and_12 (and_12_out, Q2_qn, Q0_qn, A);
  and and_13 (and_13_out, Q2_q, Q1_q, A, not_1_out);
  and and_14 (and_14_out, Q2_q, Q0_q, A, B);
  and and_15 (and_15_out, Q2_q, Q1_qn, Q0_qn, not_2_out, B);
  and and_16 (and_16_out, Q1_qn, Q0_qn, not_2_out, not_1_out);
  and and_17 (and_17_out, Q2_qn, Q1_qn, Q0_qn);
  and and_18 (and_18_out, Q2_q, Q1_qn, Q0_q, not_2_out, B);
  and and_19 (and_19_out, Q2_q, Q1_q, Q0_q, B, A);
  and and_20 (and_20_out, Q2_q, Q1_q, Q0_qn, A, not_1_out);
  or or_2 (or_2_out, and_4_out, and_5_out, and_6_out, and_7_out, and_8_out, and_9_out);
  and D1 (D1_out, ENABLE, or_3_out);
  or or_3 (or_3_out, and_10_out, and_11_out, and_12_out, and_13_out, and_14_out, and_15_out);
  and D2 (D2_out, ENABLE, or_4_out);
  or or_4 (or_4_out, and_16_out, and_17_out, and_18_out, and_19_out, and_20_out);
  and and_21 (VALID, Q2_qn, or_1_out);
  and D0 (D0_out, ENABLE, or_2_out);

  // Notes on the sheet:
  //   Q2' Q1' Q0
  //   Q2' ( Q1' Q0 + Q1 Q0' )
endmodule
