// Logisim project Lab 7.circ as structural Verilog: 3 circuits, main circuit main
module main (
  input  in_1,
  output _1001
);

  wire and_2_out, and_3_out, and_4_out, and_5_out, clock_1_out, d_ff_1_q, d_ff_1_qn, d_ff_2_q, d_ff_2_qn,
       d_ff_3_q, not_1_out, or_1_out, or_2_out, xor_1_out;

  Clock clock_1 (.out(clock_1_out));
  not not_1 (not_1_out, in_1);
  D_Flip_Flop d_ff_1 (.clk(clock_1_out), .D(in_1), .Q(d_ff_1_q), .Qn(d_ff_1_qn));  // open: preset, en, reset
  D_Flip_Flop d_ff_2 (.clk(clock_1_out), .D(or_1_out), .Q(d_ff_2_q), .Qn(d_ff_2_qn));  // open: preset, en, reset
  D_Flip_Flop d_ff_3 (.clk(clock_1_out), .D(or_2_out), .Q(d_ff_3_q));  // open: Qn, preset, en, reset
  xor xor_1 (xor_1_out, d_ff_1_q, d_ff_3_q);
  and and_1 (_1001, xor_1_out, d_ff_2_q);
  and and_2 (and_2_out, d_ff_3_q, d_ff_2_qn, d_ff_1_qn, in_1);
  and and_3 (and_3_out, d_ff_1_q, not_1_out);
  and and_4 (and_4_out, d_ff_2_q, d_ff_1_qn);
  or or_1 (or_1_out, and_2_out, and_3_out);
  and and_5 (and_5_out, and_3_out, d_ff_3_q);
  or or_2 (or_2_out, and_5_out, and_4_out);

  // Notes on the sheet:
  //   Q0
  //   Q1
  //   Q2
  //   1010
endmodule

module Moore_Device (
  input  IN,
  output UNLOCK
);

  wire and_1_out, and_2_out, and_3_out, and_4_out, and_6_out, and_7_out, and_8_out, and_9_out, and_10_out,
       clock_1_out, D0_out, D1_out, D2_out, not_1_out, or_1_out, or_2_out, or_3_out, Q0_q, Q0_qn, Q1_q,
       Q1_qn, Q2_q, Q2_qn;

  Clock clock_1 (.out(clock_1_out));
  not not_1 (not_1_out, IN);
  D_Flip_Flop Q0 (.clk(clock_1_out), .D(D0_out), .Q(Q0_q), .Qn(Q0_qn));  // open: preset, en, reset
  D_Flip_Flop Q1 (.clk(clock_1_out), .D(D1_out), .Q(Q1_q), .Qn(Q1_qn));  // open: preset, en, reset
  D_Flip_Flop Q2 (.clk(clock_1_out), .D(D2_out), .Q(Q2_q), .Qn(Q2_qn));  // open: preset, en, reset
  and and_1 (and_1_out, Q0_qn, Q1_qn);
  and and_2 (and_2_out, Q0_q, Q1_q);
  and and_3 (and_3_out, Q0_qn, IN);
  and and_4 (and_4_out, Q0_q, not_1_out);
  and and_5 (UNLOCK, Q2_q, or_1_out);
  or or_1 (or_1_out, and_1_out, and_2_out);
  and and_6 (and_6_out, Q2_q, Q1_qn, Q0_q);
  and and_7 (and_7_out, Q0_q, IN);
  and and_8 (and_8_out, Q2_qn, Q0_q);
  and and_9 (and_9_out, Q1_qn, Q0_q);
  and and_10 (and_10_out, Q2_q, Q1_q, IN);
  or or_2 (or_2_out, Q1_q, Q2_q);
  or or_3 (or_3_out, and_3_out, and_4_out);
  or D0 (D0_out, IN, and_6_out);
  or D1 (D1_out, and_7_out, and_8_out, and_9_out, and_10_out);
  and D2 (D2_out, or_2_out, or_3_out);

  // Notes on the sheet:
  //   Q2(Q1'Q0' + Q1Q0)
  //   IN + Q2Q1'Q0
  //   (Q1+Q2)(Q0'IN + Q0IN')
  //   Q0IN + Q2'Q0 + Q1'Q0 + Q2Q1IN
endmodule

module Mealy_Device (
  input  IN,
  output UNLOCK
);

  wire and_1_out, and_2_out, and_3_out, and_4_out, and_5_out, and_6_out, and_7_out, and_8_out, clock_1_out,
       D0_out, D1_out, D2_out, not_1_out, or_2_out, Q0_q, Q0_qn, Q1_q, Q1_qn, Q2_q, Q2_qn;

  Clock clock_1 (.out(clock_1_out));
  not not_1 (not_1_out, IN);
  D_Flip_Flop Q0 (.clk(clock_1_out), .D(D0_out), .Q(Q0_q), .Qn(Q0_qn));  // open: preset, en, reset
  D_Flip_Flop Q1 (.clk(clock_1_out), .D(D1_out), .Q(Q1_q), .Qn(Q1_qn));  // open: preset, en, reset
  D_Flip_Flop Q2 (.clk(clock_1_out), .D(D2_out), .Q(Q2_q), .Qn(Q2_qn));  // open: preset, en, reset
  and and_1 (and_1_out, Q2_q, Q1_q, Q0_qn, IN);
  and and_2 (and_2_out, Q2_q, Q1_qn, Q0_q, not_1_out);
  and and_3 (and_3_out, Q1_q, Q0_qn);
  and and_4 (and_4_out, Q1_qn, Q0_q);
  or or_1 (UNLOCK, and_1_out, and_2_out);
  and D0 (D0_out, IN, or_2_out);
  or or_2 (or_2_out, Q2_qn, and_3_out, and_4_out);
  and and_5 (and_5_out, Q2_qn, Q0_q);
  or D1 (D1_out, and_5_out, and_6_out);
  and and_6 (and_6_out, Q1_qn, Q0_q);
  and and_7 (and_7_out, Q1_q, Q0_qn, IN);
  or D2 (D2_out, and_7_out, and_8_out);
  and and_8 (and_8_out, Q2_qn, Q1_q, Q0_q, not_1_out);

  // Notes on the sheet:
  //   IN(Q2' + Q1Q0' + Q1'Q0)
  //   Q2'Q0 + Q1'Q0
  //   Q2Q1Q0'IN + Q2Q1'Q0IN'
  //   Q1Q0'IN + Q2'Q1Q0IN'
endmodule
