// Logisim project Lab 8.circ as structural Verilog: 1 circuit, main circuit main
module main (
  input  [3:0] IN,
  input  [1:0] F,
  output [3:0] OUT
);

  wire and_1_out, and_2_out, and_3_out, and_4_out, clock_1_out, D0_q, D0_qn, D1_q, D1_qn, GO_out, or_1_out;
  wire [3:0] A_q, adder_1_out, multiplexer_1_out, multiplier_1_out, subtractor_1_out;

  Button GO (.out(GO_out));
  Clock clock_1 (.out(clock_1_out));
  D_Flip_Flop D0 (.clk(clock_1_out), .D(and_1_out), .Q(D0_q), .Qn(D0_qn));  // open: preset, en, reset
  D_Flip_Flop D1 (.clk(clock_1_out), .D(and_4_out), .Q(D1_q), .Qn(D1_qn));  // open: preset, en, reset
  and and_1 (and_1_out, D0_qn, D1_qn, GO_out);
  and and_2 (and_2_out, D1_qn, D0_q);
  or or_1 (or_1_out, and_2_out, and_3_out);
  and and_3 (and_3_out, D1_q, D0_qn);
  and and_4 (and_4_out, GO_out, or_1_out);
  Register #(.width(4)) A (.D(OUT), .Q(A_q), .clk(clock_1_out));  // open: en, clr
  Adder #(.width(4)) adder_1 (.a(A_q), .b(IN), .out(adder_1_out));  // open: cin, cout
  Subtractor #(.width(4)) subtractor_1 (.a(A_q), .b(IN), .out(subtractor_1_out));  // open: bin, bout
  Multiplier #(.width(4)) multiplier_1 (.a(A_q), .b(IN), .out(multiplier_1_out));  // open: cin, cout
  Multiplexer #(.select(2), .width(4)) multiplexer_1 (
    .in0(IN), .in1(adder_1_out), .in2(subtractor_1_out), .in3(multiplier_1_out), .out(multiplexer_1_out),
    .sel(F));  // open: en
  Multiplexer #(.width(4)) multiplexer_2 (.in0(A_q), .in1(multiplexer_1_out), .out(OUT), .sel(and_2_out));  // open: en

  // Notes on the sheet:
  //   Z
endmodule
