// Logisim project Lab 9.circ as structural Verilog: 1 circuit, main circuit main
module main (
  input  CARDETECT,
  input  RESET,
  output HLR,
  output HLY,
  output HLG,
  output [2:0] HL_OUT,
  output FLR,
  output FLY,
  output FLG,
  output [2:0] FL_OUT
);

  wire and_1_out, and_2_out, and_3_out, and_4_out, and_5_out, clock_1_out, comparator_1_eq, comparator_2_eq,
       nor_1_out, not_1_out, not_2_out, not_3_out, not_4_out, or_1_out, or_2_out, Q0_qn, Q1_qn, xnor_1_out,
       xor_1_out;
  wire [1:0] Q0_q;
  wire [5:0] multiplexer_1_out, Right_of_Way_q, Yellow_q;

  not not_1 (not_1_out, comparator_1_eq);
  Comparator #(.width(6)) comparator_1 (.a(6'b001111), .b(Right_of_Way_q), .eq(comparator_1_eq));  // open: gt, lt
  not not_2 (not_2_out, comparator_2_eq);
  Comparator #(.width(6)) comparator_2 (.a(6'b000010), .b(Yellow_q), .eq(comparator_2_eq));  // open: gt, lt
  and and_1 (and_1_out, not_1_out, and_5_out);
  nor nor_1 (nor_1_out, and_1_out, and_2_out);
  and and_2 (and_2_out, xor_1_out, not_2_out);
  Clock clock_1 (.out(clock_1_out));
  not not_3 (not_3_out, CARDETECT);
  not not_4 (not_4_out, RESET);
  D_Flip_Flop Q0 (.clk(clock_1_out), .D(and_4_out), .Q(Q0_q[0]), .Qn(Q0_qn), .en(nor_1_out));  // open: preset, reset
  D_Flip_Flop Q1 (.clk(clock_1_out), .D(and_3_out), .Q(Q0_q[1]), .Qn(Q1_qn), .en(nor_1_out));  // open: preset, reset
  or or_1 (or_1_out, CARDETECT, Q0_q[0]);
  and and_3 (and_3_out, Q0_q[0], not_4_out);
  and and_4 (and_4_out, Q1_qn, not_4_out, or_1_out);
  or or_2 (or_2_out, not_3_out, RESET);
  xnor xnor_1 (xnor_1_out, Q0_q[0], Q0_q[1]);
  and and_5 (and_5_out, xnor_1_out, not_4_out, CARDETECT);
  xor xor_1 (xor_1_out, Q0_q[0], Q0_q[1]);
  Counter #(.width(6), .max('hf)) Right_of_Way (
    .load(or_2_out), .D({6{1'b0}}), .count(and_5_out), .Q(Right_of_Way_q), .clk(clock_1_out));  // open: carry, clr
  Counter #(.width(6), .max('h3)) Yellow (
    .count(xor_1_out), .Q(Yellow_q), .clk(clock_1_out));  // open: load, D, carry, clr
  Multiplexer #(.select(2), .width(6)) multiplexer_1 (
    .in0(6'b001100), .in1(6'b010100), .in2(6'b100010), .in3(6'b100001), .out(multiplexer_1_out), .sel(Q0_q));  // open: en
  Register #(.width(3)) HL (.D(multiplexer_1_out[5:3]), .Q(HL_OUT), .clk(clock_1_out));  // open: en, clr
  Register #(.width(3)) FL (.D(multiplexer_1_out[2:0]), .Q(FL_OUT), .clk(clock_1_out));  // open: en, clr
  LED led_1 (.in(HL_OUT[2]));
  LED led_2 (.in(HL_OUT[1]));
  LED led_3 (.in(HL_OUT[0]));
  LED led_4 (.in(FL_OUT[2]));
  LED led_5 (.in(FL_OUT[1]));
  LED led_6 (.in(FL_OUT[0]));

  assign FLG = FL_OUT[0];
  assign FLR = FL_OUT[2];
  assign FLY = FL_OUT[1];
  assign HLG = HL_OUT[0];
  assign HLR = HL_OUT[2];
  assign HLY = HL_OUT[1];
endmodule
